# Fritzing sketch low_poly_racing (saved by Fritzing 0.9.5d)
breadboards: 1

parts:
  Part1 = Arduino Uno (Rev3)
  LED1 = LED - 5mm [color="Red (633nm)" package="5 mm [THT]"]
  R5 = Resistor [tolerance=±5% resistance=10k package=THT]
  LED2 = LED - 5mm [color="Red (633nm)" package="5 mm [THT]"]
  LED3 = LED - 5mm [color="Green (555nm)" package="5 mm [THT]"]
  R6 = Resistor [tolerance=±5% resistance=10k package=THT]
  R7 = Resistor [tolerance=±5% resistance=10k package=THT]
  J1 = Piezo Speaker
  J2 = Basic Servo
  J3 = Basic Servo

nets:
  N1: Part1.D8, J1.pin2
  N2: Part1.D10_PWM/SS, LED1.anode
  N3: Part1.D11_PWM/MOSI, LED2.anode
  N4: Part1.D12/MISO, LED3.anode
  N5: Part1.D3_PWM, J2.pulse
  N6: Part1.D4, J3.pulse
  VCC: Part1.5V, J2.vcc, J3.vcc
  GND: Part1.GND, R5.Pin_1, R6.Pin_1, R7.Pin_1, J1.pin1, J2.gnd, J3.gnd
  N7: LED1.cathode, R5.Pin_0
  N8: LED2.cathode, R6.Pin_0
  N9: LED3.cathode, R7.Pin_0
