# Fritzing sketch paper_airplane (saved by Fritzing 0.9.5d)
breadboards: 1

parts:
  Part1 = Arduino Uno (Rev3)
  S1 = Pushbutton [package="[THT]"]
  LED1 = LED - 5mm [color="Red (633nm)" package="5 mm [THT]"]
  R1 = Photocell (LDR) [package=THT]
  R2 = Rotary Potentiometer (Small) [maximum_resistance=100kΩ package=THT]
  HC-SR04_Sensor_1 = HC-SR04 Ultrasonic Distance Sensor
  R3 = Resistor [tolerance=±5% resistance=1k package=THT]
  R4 = Resistor [tolerance=±5% resistance=10k package=THT]
  R5 = Resistor [tolerance=±5% resistance=1k package=THT]

nets:
  N1: Part1.A4/SDA, R2.wiper
  N2: Part1.A5/SCL, R1.pin_1, R4.Pin_0
  N3: Part1.D8, LED1.anode
  N4: Part1.D11_PWM/MOSI, HC-SR04_Sensor_1.TRIG
  N5: Part1.D12/MISO, HC-SR04_Sensor_1.ECHO
  5V: Part1.5V, S1.Pin_3, S1.Pin_4, R1.pin_0, R2.leg2, HC-SR04_Sensor_1.VCC
  GND: Part1.GND, R2.leg1, HC-SR04_Sensor_1.GND, R3.Pin_1, R4.Pin_1, R5.Pin_1
  N6: S1.Pin_1, S1.Pin_2, R3.Pin_0
  N7: LED1.cathode, R5.Pin_0
